// Logisim project primeiroCircuito.circ as structural Verilog: 1 circuit, main circuit main
module main (
  input  A,
  input  B,
  input  C,
  input  D,
  output out_5
);

  wire and_1_out, or_1_out, or_2_out;

  or or_1 (or_1_out, A, B);
  buf and_1 (and_1_out, C);  // AND_Gate
  or or_2 (or_2_out, B, D);
  and and_2 (out_5, or_1_out, and_1_out, or_2_out);

  // Notes on the sheet:
  //   ( A + B )
  //   C
  //   ( B + D )
  //   ( A + B ) * C * ( B + D )
endmodule
