// Logisim project terceiroCircuitoTabelaVerdadeExpressao.circ as structural Verilog: 1 circuit, main circuit main
module main (
  input  A,
  input  B,
  input  C,
  input  D,
  output out_5
);

  wire and_1_out, and_2_out, and_3_out, and_4_out, and_5_out, not_1_out, not_2_out, not_3_out, not_4_out,
       not_5_out, not_6_out, not_7_out, not_8_out, not_9_out, not_10_out, or_1_out, or_2_out, or_3_out,
       xor_1_out;

  not not_1 (not_1_out, B);
  and and_1 (and_1_out, not_1_out, C, not_2_out);
  not not_2 (not_2_out, D);
  not not_3 (not_3_out, A);
  or or_1 (or_1_out, not_3_out, B);
  xor xor_1 (xor_1_out, A, B);
  not not_4 (not_4_out, or_1_out);
  not not_5 (not_5_out, B);
  not not_6 (not_6_out, A);
  not not_7 (not_7_out, D);
  not not_8 (not_8_out, or_2_out);
  or or_2 (or_2_out, xor_1_out, and_1_out);
  and and_2 (and_2_out, not_4_out, D);
  and and_3 (and_3_out, not_5_out, C);
  and and_4 (and_4_out, not_6_out, not_7_out);
  or or_3 (or_3_out, and_2_out, and_3_out, not_9_out);
  not not_9 (not_9_out, D);
  not not_10 (not_10_out, or_3_out);
  and and_5 (and_5_out, not_8_out, not_10_out);
  or or_4 (out_5, and_5_out, and_4_out);
endmodule
